# Fritzing sketch Esquema (saved by Fritzing 0.9.3b)
breadboards: 1

parts:
  DS18B20 = DS18B20 1-Wire Temperature Sensor Probe Cable
  lcd_keypad_shield = LCD Keypad Shield
  Componente3 = Arduino Uno (Rev3)
  R1 = Resistor [tolerance=±5% resistance=470 package=THT]

nets:
  GND: DS18B20.GND, lcd_keypad_shield.GND, Componente3.GND
  N1: DS18B20.DQ, DS18B20.VDD
  N2: lcd_keypad_shield.D11_MOSI, Componente3.D5_PWM
  N3: lcd_keypad_shield.D12_MISO, Componente3.D6_PWM
  N4: lcd_keypad_shield.D13_SCK, Componente3.D7
  N5: lcd_keypad_shield.D3, Componente3.D4
  N6: lcd_keypad_shield.RESET, Componente3.RESET
  +3V3: lcd_keypad_shield.+3V3, Componente3.3V3
  +5V: lcd_keypad_shield.+5V, Componente3.5V
  VIN: lcd_keypad_shield.VIN, Componente3.VIN
  N7: R1.Pin_0, R1.Pin_1

notes:
  Normalmente apenas 3 fios sendo
  amarelo,preto,vermelho

custom parts:
  LCD Keypad Shield: It consists of a 1602 white character blue backlight LCD. The keypad consists of 5 keys — select, up, right, down and left. To save the digital IO pins, the keypad interface uses only one ADC channel. The key value is read through a 5 stage voltage divider.
